// Logisim project drugi_domaci.circ as structural Verilog: 2 circuits, main circuit NILI kolo
module NILI_kolo (
  input  x1___16,
  input  x2___8,
  input  x3___4,
  input  x4___2,
  input  x5___1,
  output y
);

  wire nor_1_out, nor_2_out, nor_3_out, nor_4_out, nor_5_out, nor_6_out, nor_7_out, nor_8_out, nor_9_out;

  nor nor_1 (nor_1_out, x2___8, x2___8);
  nor nor_2 (nor_2_out, x1___16, nor_1_out);
  nor nor_3 (nor_3_out, x5___1, x5___1);
  nor nor_4 (nor_4_out, nor_2_out, nor_2_out);
  nor nor_5 (nor_5_out, x3___4, x3___4);
  nor nor_6 (nor_6_out, x4___2, nor_3_out);
  nor nor_7 (nor_7_out, nor_4_out, nor_5_out);
  nor nor_8 (nor_8_out, nor_7_out, nor_7_out);
  nor nor_9 (nor_9_out, nor_6_out, nor_6_out);
  nor nor_10 (y, nor_8_out, nor_9_out);

  // Notes on the sheet:
  //   Datum rođenja: 17.05.
  //   Zbir cifara: 1+7+0+5 = 13
endmodule

module I_i_NOT (
  input  x1,
  input  x2,
  input  x3,
  input  x4,
  input  x5,
  output y
);

  wire and_1_out, and_2_out, and_4_out, not_1_out, not_2_out;

  not not_1 (not_1_out, x1);
  and and_1 (and_1_out, not_1_out, x2);
  not not_2 (not_2_out, x4);
  and and_2 (and_2_out, and_1_out, x3);
  and and_3 (y, and_2_out, and_4_out);
  and and_4 (and_4_out, not_2_out, x5);
endmodule
